// Logisim project main.circ as structural Verilog: 5 circuits, main circuit main
module main (
  input  [3:0] in_1,
  input  [3:0] in_2,
  input  in_3,
  output out_4,
  output [3:0] out_5
);

  _4_Bit_Ripple_Carry_Adder u_4_bit_ripple_carry_adder_1 (.CO(out_4), .O(out_5), .A(in_1), .B(in_2), .CI(in_3));
endmodule

module Full_Adder (
  input  A,
  input  B,
  input  CI,
  output S,
  output CO
);

  wire and_1_out, and_2_out, or_1_out, xor_1_out;

  xor xor_1 (xor_1_out, A, B);
  and and_1 (and_1_out, CI, or_1_out);
  or or_1 (or_1_out, A, B);
  and and_2 (and_2_out, A, B);
  xor xor_2 (S, xor_1_out, CI);
  or or_2 (CO, and_1_out, and_2_out);
endmodule

module _4_Bit_Ripple_Carry_Adder (
  input  [3:0] A,
  input  CI,
  input  [3:0] B,
  output CO,
  output [3:0] O
);

  wire full_adder_2_co, full_adder_3_co, full_adder_4_co;

  Full_Adder full_adder_1 (.S(O[3]), .CO(CO), .B(B[3]), .CI(full_adder_2_co), .A(A[3]));
  Full_Adder full_adder_2 (.S(O[2]), .CO(full_adder_2_co), .B(B[2]), .CI(full_adder_3_co), .A(A[2]));
  Full_Adder full_adder_3 (.S(O[1]), .CO(full_adder_3_co), .B(B[1]), .CI(full_adder_4_co), .A(A[1]));
  Full_Adder full_adder_4 (.S(O[0]), .CO(full_adder_4_co), .B(B[0]), .CI(CI), .A(A[0]));
endmodule

module _4_Bit_Carry_Lookahead_Generator (
  input  [3:0] A,
  input  [3:0] B,
  input  CI,
  output [3:0] CO,
  output [3:0] P
);

  wire and_1_out, and_2_out, and_3_out, and_4_out, and_5_out, and_6_out, and_7_out, and_8_out, and_9_out,
       and_10_out, G0_out, G1_out, G2_out, G3_out;

  and G0 (G0_out, B[0], A[0]);
  and G1 (G1_out, B[1], A[1]);
  and G2 (G2_out, B[2], A[2]);
  and G3 (G3_out, B[3], A[3]);
  xor P0 (P[0], B[0], A[0]);
  xor P1 (P[1], B[1], A[1]);
  xor P2 (P[2], B[2], A[2]);
  xor p3 (P[3], B[3], A[3]);
  and and_1 (and_1_out, CI, P[0]);
  or or_1 (CO[0], and_1_out, G0_out);
  and and_2 (and_2_out, CI, P[0], P[1]);
  and and_3 (and_3_out, G0_out, P[1]);
  or or_2 (CO[1], and_2_out, and_3_out, G1_out);
  and and_4 (and_4_out, CI, P[0], P[1], P[2]);
  and and_5 (and_5_out, G0_out, P[1], P[2]);
  and and_6 (and_6_out, G1_out, P[2]);
  or or_3 (CO[2], and_4_out, and_5_out, and_6_out, G2_out);
  and and_7 (and_7_out, CI, P[0], P[1], P[2], P[3]);
  and and_8 (and_8_out, G1_out, P[2], P[3]);
  and and_9 (and_9_out, G2_out, P[3]);
  and and_10 (and_10_out, G0_out, P[1], P[2], P[3]);
  or or_4 (CO[3], and_7_out, and_10_out, and_8_out, and_9_out, G3_out);
endmodule

module _4_Bit_Carry_Lookahead_Adder (
  input  [3:0] in_1,
  input  [3:0] in_2,
  input  in_3,
  output CO,
  output [3:0] O
);

  wire [2:0] n4_bit_carry_lookahead_generator_1_co;
  wire [3:0] n4_bit_carry_lookahead_generator_1_p;

  _4_Bit_Carry_Lookahead_Generator u_4_bit_carry_lookahead_generator_1 (
    .CO({CO, n4_bit_carry_lookahead_generator_1_co}), .P(n4_bit_carry_lookahead_generator_1_p), .B(in_2),
    .CI(in_3), .A(in_1));
  xor xor_1 (O[3], n4_bit_carry_lookahead_generator_1_p[3], n4_bit_carry_lookahead_generator_1_co[2]);
  xor xor_2 (O[2], n4_bit_carry_lookahead_generator_1_p[2], n4_bit_carry_lookahead_generator_1_co[1]);
  xor xor_3 (O[1], n4_bit_carry_lookahead_generator_1_p[1], n4_bit_carry_lookahead_generator_1_co[0]);
  xor xor_4 (O[0], n4_bit_carry_lookahead_generator_1_p[0], in_3);
endmodule
